# Fritzing sketch rpi_DHT22_soil_moisture_perfboard (saved by Fritzing 0.9.3b)
perfboards: 1

parts:
  U1 = MCP3008 [package=dil16]
  Raspberry_Pi_1 = Raspberry Pi 3 [part_number=RPI-3-V1.2]
  Bauteil1 = FC-28 Soil Hygrometer Module
  Bauteil2 = FC-28 Soil Hygrometer Module - Probe
  DHT1 = DHT22 Humidity and Temperature Sensor
  LED1 = smd LED [color="Green (555nm)" package="0603 [SMD]"]
  R2 = Resistor [tolerance=±5% resistance=10k package="0603 [SMD]"]  # not connected
  LED2 = smd LED [color="Red (633nm)" package="0603 [SMD]"]
  J3 = double row male pin header, 4 pins [form="♂ (male)"]
  J1 = male pin header, 2 pins [form="♂ (male)"]
  J4 = male pin header, 3 pins [form="♂ (male)"]
  J5 = female pin header, 2 pins [form="♀ (female)"]
  J6 = female pin header, 2 pins [form="♀ (female)"]
  J7 = male pin header, 3 pins [form="♂ (male)"]
  J8 = male pin header, 3 pins [form="♂ (male)"]
  J9 = male pin header, 3 pins [form="♂ (male)"]
  J10 = male pin header, 3 pins [form="♂ (male)"]
  R1 = Resistor [tolerance=±1% resistance=200 package=THT]
  R3 = Resistor [tolerance=±1% resistance=100 package=THT]

nets:
  N1: U1.CH0, Bauteil1.AO, J7.pin3
  N2: U1.CH3, J8.pin3
  N3: U1.CH6, J9.pin3
  N4: U1.CS/SHDN, Raspberry_Pi_1.GPIO8, J3.pin1
  N5: U1.D-In, Raspberry_Pi_1.GPIO10, J3.pin2
  N6: U1.D-Out, Raspberry_Pi_1.GPIO9, J3.pin3
  N7: U1.CLK, Raspberry_Pi_1.GPIO11, J3.pin4
  3V3: U1.V-REF, U1.V-DD, Raspberry_Pi_1.3v3, Bauteil1.VCC, J1.pin1, J7.pin1, J8.pin1, J9.pin1
  N8: Raspberry_Pi_1.GPIO17, DHT1.DATA, J4.pin1, J10.pin2
  GND: Raspberry_Pi_1.GPIO6, Raspberry_Pi_1.GND, Bauteil1.GND, LED1.cathode, J1.pin2, J5.pin2, J7.pin2, J8.pin2, J9.pin2
  N9: Raspberry_Pi_1.GPIO18, J4.pin3, R3.Pin_0
  N10: Raspberry_Pi_1.GPIO14, J4.pin2, R1.Pin_0
  N11: Bauteil1.POS, Bauteil2.POS
  N12: Bauteil1.NEG, Bauteil2.NEG
  N13: DHT1.VDD, J10.pin3
  N14: DHT1.GND, J10.pin1
  N15: LED1.anode, J5.pin1, R1.Pin_1
  N16: LED2.cathode, J6.pin2
  N17: LED2.anode, J6.pin1, R3.Pin_1

custom parts:
  FC-28 Soil Hygrometer Module: The FC-28 is a soil hygrometer module that uses the Texas Instruments LM393 comparator chip to provide an analog measurement of soil humidity. The digital output is high when soil moisture is over a certain threshold, as determined by adjusting the potentiometer.
  FC-28 Soil Hygrometer Module - Probe: The FC-28 is a soil hygrometer module that uses the Texas Instruments LM393 comparator chip to provide an analog measurement of soil humidity.
